# Fritzing sketch lickometer_pcb-simple (saved by Fritzing 0.9.3b)
breadboards: 1

parts:
  transistor = NPN-Transistor [package="TO92 [THT]"]
  LED = LED - 3mm [color="Red (633nm)" package="3 mm [THT]"]
  probe_+ = female pin header, 1 pin [form="♀ (female)"]
  probe = female pin header, 1 pin [form="♀ (female)"]
  battary_+ = Battery Holders [package=battcom_20mm_pth]

nets:
  N1: transistor.E, battary_+.-
  N2: transistor.B, probe.pin1
  N3: transistor.C, LED.cathode
  N4: LED.anode, probe_+.pin1, battary_+.+
